# Fritzing sketch teamproject (saved by Fritzing 0.9.4)
breadboards: 1
perfboards: 1

parts:
  RP1 = XIAO RP2040 [package="DIP (Dual Inline) [THT]"]
  LLC1 = Logic Level Converter [package="Breakout board"]
  RP6 = XIAO RP2040 [package="DIP (Dual Inline) [THT]"]
  LLC6 = Logic Level Converter [package="Breakout board"]

nets:
  N1: RP1.D4, LLC1.LV1
  N2: RP1.D5, LLC1.LV2
  N3: RP1.3V3, LLC1.LV
  N4: RP1.GND, LLC1.L-GND, LLC1.H-GND
  N5: RP1.5V, LLC1.HV
  N6: RP6.D7, LLC6.LV2
  N7: RP6.D8, LLC6.LV1
  N8: RP6.3V3, LLC6.LV
  N9: LLC6.L-GND, LLC6.H-GND

custom parts:
  XIAO RP2040: Seeed Studio XIAO RP2040 is compatible with the Raspberry Pi RP2040 ecosystem as they share the same RP2040 chip. It supports multiple languages including C / MicroPython / CircuitPython. This will be a great tool for you to get started with MicroPython.
  Logic Level Converter: 5V to/from 3.3V logic level converter
